// Logisim project ALU.circ as structural Verilog: 1 circuit, main circuit ALU
module ALU (
  input  [31:0] A,
  input  [31:0] B,
  input  [4:0] Shift,
  input  [3:0] Codop,
  input  CarryIn,
  output [31:0] S,
  output [3:0] Flags
);

  wire adder_1_cout, and_1_out, and_2_out, and_6_out, bitselector_1_out, multiplexer_4_out, not_2_out,
       or_2_out, subtractor_1_bout, xor_2_out, xor_3_out;
  wire [1:0] multiplexer_5_out;
  wire [4:0] multiplexer_7_out, subtractor_2_out, subtractor_3_out;
  wire [31:0] adder_1_out, and_3_out, and_4_out, and_5_out, multiplexer_1_out, multiplexer_2_out,
       multiplexer_3_out, multiplier_1_out, negator_1_out, not_1_out, or_1_out, shifter_1_out, shifter_2_out,
       shifter_3_out, shifter_4_out, subtractor_1_out, xor_1_out;

  Multiplexer #(.width(32), .enable("false")) multiplexer_1 (.in0(B), .in1(A), .out(multiplexer_1_out), .sel(Codop[3]));
  Multiplexer #(.width(32), .enable("false")) multiplexer_2 (.in0(A), .in1(B), .out(multiplexer_2_out), .sel(Codop[3]));
  and and_1 (and_1_out, Codop[2], CarryIn);
  and and_2 (and_2_out, Codop[2], ~CarryIn);  // AND_Gate
  assign and_3_out = A & B;  // AND_Gate and_3, 32 bits wide
  assign xor_1_out = A ^ B;  // XOR_Gate xor_1, 32 bits wide
  Shifter #(.width(32)) shifter_1 (.in(B), .\dist (Shift), .out(shifter_1_out));
  Shifter #(.width(32), .shift("lr")) shifter_2 (.in(B), .\dist (Shift), .out(shifter_2_out));
  Shifter #(.width(32), .shift("ar")) shifter_3 (.in(B), .\dist (Shift), .out(shifter_3_out));
  Adder #(.width(32)) adder_1 (.a(A), .b(B), .out(adder_1_out), .cin(and_1_out), .cout(adder_1_cout));
  Subtractor #(.width(32)) subtractor_1 (
    .a(multiplexer_1_out), .b(multiplexer_2_out), .out(subtractor_1_out), .bin(and_2_out),
    .bout(subtractor_1_bout));
  Shifter #(.width(32), .shift("rr")) shifter_4 (.in(B), .\dist (Shift), .out(shifter_4_out));
  assign and_4_out = A & B;  // AND_Gate and_4, 32 bits wide
  Negator #(.width(32)) negator_1 (.in(A), .out(negator_1_out));
  assign or_1_out = A | B;  // OR_Gate or_1, 32 bits wide
  Multiplier #(.width(32)) multiplier_1 (.a(A), .b(B), .out(multiplier_1_out), .cin({32{1'b0}}));  // open: cout
  assign not_1_out = ~B;  // NOT_Gate not_1, 32 bits wide
  assign and_5_out = ~A & B;  // AND_Gate and_5, 32 bits wide
  not not_2 (not_2_out, Codop[0]);
  Multiplexer #(.select(4), .width(32), .enable("false")) multiplexer_3 (
    .in0(and_3_out), .in1(xor_1_out), .in2(shifter_1_out), .in3(shifter_2_out), .in4(shifter_3_out),
    .in5(adder_1_out), .in6(subtractor_1_out), .in7(shifter_4_out), .in8(and_4_out), .in9(negator_1_out),
    .in10(subtractor_1_out), .in11(adder_1_out), .in12(or_1_out), .in13(multiplier_1_out), .in14(and_5_out),
    .in15(not_1_out), .out(multiplexer_3_out), .sel(Codop));
  Multiplexer #(.enable("false")) multiplexer_4 (
    .in0(adder_1_cout), .in1(subtractor_1_bout), .out(multiplexer_4_out), .sel(not_2_out));
  // Probe on multiplexer_3_out
  Multiplexer #(.select(4), .width(2), .enable("false")) multiplexer_5 (
    .in0(2'b00), .in1(2'b00), .in2(2'b10), .in3(2'b10), .in4(2'b00), .in5(2'b01), .in6(2'b01), .in7(2'b10),
    .in8(2'b00), .in9(2'b00), .in10(2'b01), .in11(2'b01), .in12(2'b00), .in13(2'b00), .in14(2'b00),
    .in15(2'b00), .out(multiplexer_5_out), .sel(Codop));
  or or_2 (or_2_out, ~Codop[0], Codop[1]);  // OR_Gate
  Subtractor #(.width(5)) subtractor_2 (.a({5{1'b0}}), .b(Shift), .out(subtractor_2_out));  // open: bin, bout
  Subtractor #(.width(5)) subtractor_3 (.a(Shift), .b(5'b00001), .out(subtractor_3_out));  // open: bin, bout
  Multiplexer #(.width(32), .enable("false")) multiplexer_6 (
    .in0(multiplexer_3_out), .in1(B), .out(S), .sel(and_6_out));
  and and_6 (and_6_out, or_2_out, ~Codop[2], Codop[3]);  // AND_Gate
  Comparator #(.width(32)) comparator_1 (
    .a(multiplexer_3_out), .b({32{1'b0}}), .eq(Flags[2]), .lt(Flags[3]));  // open: gt
  xor xor_2 (xor_2_out, Flags[3], B[31]);
  ExactlyOne xor_3 (.out(xor_3_out), .in0(B[31]), .in1(Codop[0]), .in2(A[31]));
  BitSelector #(.width(32)) bitselector_1 (.in(B), .out(bitselector_1_out), .sel(multiplexer_7_out));
  Multiplexer #(.width(5), .enable("false")) multiplexer_7 (
    .in0(subtractor_2_out), .in1(subtractor_3_out), .out(multiplexer_7_out), .sel(Codop[0]));
  and and_7 (Flags[0], xor_2_out, xor_3_out, multiplexer_5_out[0]);
  Multiplexer #(.select(2), .enable("false")) multiplexer_8 (
    .in0(1'b0), .in1(multiplexer_4_out), .in2(bitselector_1_out), .out(Flags[1]), .sel(multiplexer_5_out));  // open: in3

  // Other names for the same wires on the sheet: V = Flags[0]; C = Flags[1]; Z = Flags[2]; N = Flags[3];
  //   Op[3:0] = Codop; S_t[4:0] = Shift

  // Notes on the sheet:
  //   Note: for ROR, C = N
  //   Note 2: assume that shift > 0 for LSL and LSR
  //   2=LSL
  //   1=ADC, SBC, CMP, CMN
  //   3=LSR, ROR
  //   TST, CMP, CMN
endmodule
