// Logisim project ALU_thomas.circ as structural Verilog: 1 circuit, main circuit ALU
module ALU (
  input  [31:0] A,
  input  [31:0] B,
  input  [4:0] Shift,
  input  CarryIn,
  input  [3:0] Codop,
  output [31:0] S,
  output [3:0] Flags
);

  wire adder_1_cout, adder_2_cout, bitselector_1_out, bitselector_2_out, not_1_out, OV, subtractor_1_bout,
       subtractor_3_bout, xnor_1_out, xor_1_out;
  wire [31:0] adder_1_out, adder_2_out, and_2_out, and_3_out, and_4_out, multiplier_1_out, not_2_out,
       not_3_out, not_4_out, or_1_out, shifter_1_out, shifter_2_out, shifter_3_out, shifter_4_out,
       subtractor_1_out, subtractor_2_out, subtractor_3_out, xor_2_out;

  BitSelector #(.width(32)) bitselector_1 (.in(B), .out(bitselector_1_out), .sel({5{1'b1}}));
  xnor xnor_1 (xnor_1_out, bitselector_1_out, bitselector_2_out);
  BitSelector #(.width(32)) bitselector_2 (.in(A), .out(bitselector_2_out), .sel({5{1'b1}}));
  and and_1 (OV, xnor_1_out, xor_1_out);
  not not_1 (not_1_out, CarryIn);
  assign not_2_out = ~B;  // NOT_Gate not_2, 32 bits wide
  assign not_3_out = ~A;  // NOT_Gate not_3, 32 bits wide
  xor xor_1 (xor_1_out, bitselector_2_out, Flags[0]);
  assign and_2_out = A & B;  // AND_Gate and_2, 32 bits wide
  assign xor_2_out = A ^ B;  // XOR_Gate xor_2, 32 bits wide
  Shifter #(.width(32)) shifter_1 (.in(B), .\dist (Shift), .out(shifter_1_out));
  Shifter #(.width(32), .shift("lr")) shifter_2 (.in(B), .\dist (Shift), .out(shifter_2_out));
  Shifter #(.width(32), .shift("ar")) shifter_3 (.in(B), .\dist (Shift), .out(shifter_3_out));
  Adder #(.width(32)) adder_1 (.a(A), .b(B), .out(adder_1_out), .cin(CarryIn), .cout(adder_1_cout));
  Subtractor #(.width(32)) subtractor_1 (
    .a(A), .b(B), .out(subtractor_1_out), .bin(not_1_out), .bout(subtractor_1_bout));
  Shifter #(.width(32), .shift("rr")) shifter_4 (.in(B), .\dist (Shift), .out(shifter_4_out));
  assign and_3_out = B & A;  // AND_Gate and_3, 32 bits wide
  Subtractor #(.width(32)) subtractor_2 (.a({32{1'b0}}), .b(B), .out(subtractor_2_out), .bin(1'b0));  // open: bout
  Subtractor #(.width(32)) subtractor_3 (.a(A), .b(B), .out(subtractor_3_out), .bout(subtractor_3_bout));  // open: bin
  Adder #(.width(32)) adder_2 (.a(B), .b(A), .out(adder_2_out), .cout(adder_2_cout));  // open: cin
  assign or_1_out = B | A;  // OR_Gate or_1, 32 bits wide
  Multiplier #(.width(32)) multiplier_1 (.a(B), .b(A), .out(multiplier_1_out));  // open: cin, cout
  assign and_4_out = A & not_2_out;  // AND_Gate and_4, 32 bits wide
  Multiplexer #(.select(4), .width(32), .enable("false")) multiplexer_1 (
    .in0(and_2_out), .in1(xor_2_out), .in2(shifter_1_out), .in3(shifter_2_out), .in4(shifter_3_out),
    .in5(adder_1_out), .in6(subtractor_1_out), .in7(shifter_4_out), .in8(and_3_out), .in9(subtractor_2_out),
    .in10(subtractor_3_out), .in11(adder_2_out), .in12(or_1_out), .in13(multiplier_1_out), .in14(and_4_out),
    .in15(not_3_out), .out(S), .sel(Codop));
  BitSelector #(.width(32)) bitselector_3 (.in(S), .out(Flags[0]), .sel({5{1'b1}}));
  assign not_4_out = ~S;  // NOT_Gate not_4, 32 bits wide
  Multiplexer #(.select(4), .enable("false")) multiplexer_2 (
    .in0(1'b0), .in1(1'b0), .in2(1'b0), .in3(1'b0), .in4(1'b0), .in5(adder_1_cout), .in6(subtractor_1_bout),
    .in7(1'b0), .in8(1'b0), .in9(1'b0), .in10(subtractor_3_bout), .in11(adder_2_cout), .in12(1'b0),
    .in14(1'b0), .in15(1'b0), .out(Flags[2]), .sel(Codop));  // open: in13
  Multiplexer #(.select(4), .enable("false")) multiplexer_3 (
    .in0(1'b0), .in1(1'b0), .in2(1'b0), .in3(1'b0), .in4(1'b0), .in5(OV), .in6(OV), .in7(1'b0), .in8(1'b0),
    .in9(1'b0), .in10(OV), .in11(OV), .in12(1'b0), .in13(1'b0), .in14(1'b0), .in15(1'b0), .out(Flags[3]),
    .sel(Codop));
  and and_5 (Flags[1], not_4_out[0], not_4_out[1], not_4_out[2], not_4_out[3], not_4_out[4], not_4_out[5], not_4_out[6], not_4_out[7], not_4_out[8], not_4_out[9], not_4_out[10], not_4_out[11], not_4_out[12], not_4_out[13], not_4_out[14], not_4_out[15], not_4_out[17], not_4_out[18], not_4_out[19], not_4_out[20], not_4_out[21], not_4_out[22], not_4_out[23], not_4_out[24], not_4_out[25], not_4_out[26], not_4_out[27], not_4_out[28], not_4_out[29], not_4_out[30], not_4_out[31], not_4_out[16]);

  // Other names for the same wires on the sheet: N = Flags[0]; Z = Flags[1]; C = Flags[2]; V = Flags[3]

  // Notes on the sheet:
  //   Note: for ROR, C = N
  //   Note 2: assume that shift > 0 for LSL and LSR
endmodule
