// Logisim project Controller.circ as structural Verilog: 8 circuits, main circuit Controller
module Controller (
  input  [15:0] Inst,
  input  [3:0] Flags,
  input  Clk,
  input  Reset,
  output Carry,
  output DP_Shift,
  output Imm32_Enable,
  output [4:0] Imm5,
  output [31:0] Imm32,
  output [3:0] ALU_Opcode,
  output [2:0] Rm,
  output [2:0] Rn,
  output [2:0] Rd,
  output [31:0] RAM_Addr,
  output Load,
  output Store,
  output [15:0] PC
);

  wire Conditional_1_verified, Load_Store_1_pc_hold, not_1_out, Opcode_Decoder_1_conditional,
       Opcode_Decoder_1_data_processing, Opcode_Decoder_1_load_store, Opcode_Decoder_1_shift,
       Opcode_Decoder_1_sp_address, Shift_Add_Sub_Mov_1_carry, SP_Address_1_write_enable;
  wire [2:0] Data_Processing_1_rd, Data_Processing_1_rm, Data_Processing_1_rn, Load_Store_1_rd,
       Load_Store_1_rm, Shift_Add_Sub_Mov_1_rd, Shift_Add_Sub_Mov_1_rm, Shift_Add_Sub_Mov_1_rn;
  wire [3:0] Data_Processing_1_alu_opcode, Data_Processing_1_flags_update_mask, flags_apsr_1_flags_out,
       or_1_out, Shift_Add_Sub_Mov_1_alu_opcode, Shift_Add_Sub_Mov_1_flags_update_mask;
  wire [10:0] Conditional_1_offset;
  wire [15:0] adder_1_out, adder_2_out, bit_extender_1_out;
  wire [31:0] SP_Address_1_new_stack_pointer, Stack_Pointer_q;

  Register #(.width(32)) Stack_Pointer (
    .D(SP_Address_1_new_stack_pointer), .en(SP_Address_1_write_enable), .clk(Clk), .Q(Stack_Pointer_q),
    .clr(Reset));
  Opcode_Decoder Opcode_Decoder_1 (
    .Opcode(Inst[15:10]), .Shift(Opcode_Decoder_1_shift), .Data_Processing(Opcode_Decoder_1_data_processing),
    .Load_Store(Opcode_Decoder_1_load_store), .SP_Address(Opcode_Decoder_1_sp_address),
    .Conditional(Opcode_Decoder_1_conditional));
  assign or_1_out = Data_Processing_1_flags_update_mask | Shift_Add_Sub_Mov_1_flags_update_mask;  // OR_Gate or_1, 4 bits wide
  Shift_Add_Sub_Mov Shift_Add_Sub_Mov_1 (
    .Imm32_Enable(Imm32_Enable), .Instruction(Inst), .ALU_Opcode(Shift_Add_Sub_Mov_1_alu_opcode),
    .Enable(Opcode_Decoder_1_shift), .Carry(Shift_Add_Sub_Mov_1_carry),
    .Flags_Update_Mask(Shift_Add_Sub_Mov_1_flags_update_mask), .Rd(Shift_Add_Sub_Mov_1_rd),
    .Rn(Shift_Add_Sub_Mov_1_rn), .Rm(Shift_Add_Sub_Mov_1_rm), .Imm5(Imm5), .Imm32(Imm32));
  Data_Processing Data_Processing_1 (
    .Rd(Data_Processing_1_rd), .Instruction(Inst), .Rn(Data_Processing_1_rn),
    .Enable(Opcode_Decoder_1_data_processing), .Rm(Data_Processing_1_rm),
    .ALU_Opcode(Data_Processing_1_alu_opcode), .Flags_Update_Mask(Data_Processing_1_flags_update_mask));
  Flags_APSR flags_apsr_1 (
    .Update_Mask(or_1_out), .Flags_In(Flags), .Clk(Clk), .Rst(Reset), .Flags_Out(flags_apsr_1_flags_out));
  Load_Store Load_Store_1 (
    .Rm(Load_Store_1_rm), .RAM_Addr(RAM_Addr), .Load(Load), .Rd(Load_Store_1_rd),
    .Stack_Pointer(Stack_Pointer_q), .Instruction(Inst), .Enable(Opcode_Decoder_1_load_store), .Clk(Clk),
    .PC_Hold(Load_Store_1_pc_hold), .Store(Store), .Reset(Reset));
  Conditional Conditional_1 (
    .Instruction(Inst), .Verified(Conditional_1_verified), .Enable(Opcode_Decoder_1_conditional),
    .Offset(Conditional_1_offset), .Z(flags_apsr_1_flags_out[2]), .V(flags_apsr_1_flags_out[0]),
    .N(flags_apsr_1_flags_out[3]), .C(flags_apsr_1_flags_out[1]));
  assign bit_extender_1_out = {{5{Conditional_1_offset[10]}}, Conditional_1_offset};  // Bit_Extender bit_extender_1
  SP_Address SP_Address_1 (
    .New_Stack_Pointer(SP_Address_1_new_stack_pointer), .Stack_Pointer(Stack_Pointer_q),
    .Enable(Opcode_Decoder_1_sp_address), .Instruction(Inst), .Write_Enable(SP_Address_1_write_enable));
  Adder #(.width(16)) adder_1 (.a(16'h3), .b(bit_extender_1_out), .out(adder_1_out), .cin(1'b0));  // open: cout
  Adder #(.width(16)) adder_2 (.a(adder_1_out), .b(PC), .out(adder_2_out), .cin(1'b0));  // open: cout
  and and_1 (DP_Shift, Opcode_Decoder_1_shift, ~Opcode_Decoder_1_data_processing);  // AND_Gate
  not not_1 (not_1_out, Load_Store_1_pc_hold);
  Counter #(.width(16), .max('hffff), .trigger("falling")) counter_1 (
    .clr(Reset), .load(Conditional_1_verified), .up(1'b1), .count(not_1_out), .clk(Clk), .D(adder_2_out),
    .Q(PC));  // open: carry
  Multiplexer #(.enable("false")) multiplexer_1 (
    .in0(flags_apsr_1_flags_out[1]), .in1(Shift_Add_Sub_Mov_1_carry), .out(Carry), .sel(DP_Shift));
  assign ALU_Opcode = Shift_Add_Sub_Mov_1_alu_opcode | Data_Processing_1_alu_opcode;  // OR_Gate or_2, 4 bits wide
  assign Rm = Shift_Add_Sub_Mov_1_rm | Data_Processing_1_rm | Load_Store_1_rm;  // OR_Gate or_3, 3 bits wide
  assign Rn = Shift_Add_Sub_Mov_1_rn | Data_Processing_1_rn;  // OR_Gate or_4, 3 bits wide
  assign Rd = Shift_Add_Sub_Mov_1_rd | Data_Processing_1_rd | Load_Store_1_rd;  // OR_Gate or_5, 3 bits wide

  // Notes on the sheet:
  //   Extract carry
  //   Extract Opcode
  //   IF Reg_Imm=1 THEN use shift value from register ELSE use shift value from Imm5
  //   Buffer flags for next instruction
  //   Add 3 to offset because ARM pre-increments PC
  //   and does an additionnal prefect operation
endmodule

module Conditional (
  input  Enable,
  input  [15:0] Instruction,
  input  Z,
  input  C,
  input  N,
  input  V,
  output [10:0] Offset,
  output Verified
);

  wire multiplexer_2_out, not_1_out, not_2_out, not_3_out, not_4_out, not_5_out, not_6_out, not_7_out,
       or_1_out, or_2_out, or_3_out, xor_1_out;
  wire [10:0] bit_extender_1_out, multiplexer_1_out;

  assign bit_extender_1_out = {{3{Instruction[7]}}, Instruction[7:0]};  // Bit_Extender bit_extender_1
  Multiplexer #(.width(11), .enable("false")) multiplexer_1 (
    .in0(bit_extender_1_out), .in1(Instruction[10:0]), .out(multiplexer_1_out), .sel(Instruction[13]));
  not not_1 (not_1_out, Z);
  not not_2 (not_2_out, C);
  not not_3 (not_3_out, N);
  not not_4 (not_4_out, V);
  or or_1 (or_1_out, ~C, Z);  // OR_Gate
  xor xor_1 (xor_1_out, N, V);
  // Probe on Instruction[11:8]
  not not_5 (not_5_out, or_1_out);
  not not_6 (not_6_out, xor_1_out);
  not not_7 (not_7_out, or_2_out);
  or or_2 (or_2_out, Z, xor_1_out);
  or or_3 (or_3_out, Instruction[13], multiplexer_2_out);
  Multiplexer #(.select(4), .enable("false")) multiplexer_2 (
    .in0(Z), .in1(not_1_out), .in2(C), .in3(not_2_out), .in4(N), .in5(not_3_out), .in6(V), .in7(not_4_out),
    .in8(not_5_out), .in9(or_1_out), .in10(not_6_out), .in11(xor_1_out), .in12(not_7_out), .in13(or_2_out),
    .in14(1'b1), .out(multiplexer_2_out), .sel(Instruction[11:8]));  // open: in15
  Pull_Resistor pull_resistor_1 (.node(Offset));
  assign Offset = Enable ? multiplexer_1_out : 11'bz;  // Controlled_Buffer controlled_buffer_1
  and and_1 (Verified, Enable, or_3_out);
endmodule

module Opcode_Decoder (
  input  [5:0] Opcode,
  output Shift,
  output Data_Processing,
  output Load_Store,
  output SP_Address,
  output Conditional
);

  wire and_5_out, and_6_out;

  and and_1 (Shift, ~Opcode[5], ~Opcode[4]);  // AND_Gate
  and and_2 (Data_Processing, ~Opcode[5], Opcode[4], ~Opcode[3], ~Opcode[2], ~Opcode[1], ~Opcode[0]);  // AND_Gate
  and and_3 (Load_Store, Opcode[5], ~Opcode[4], ~Opcode[3], Opcode[2]);  // AND_Gate
  and and_4 (SP_Address, Opcode[5], ~Opcode[4], Opcode[3], Opcode[2]);  // AND_Gate
  and and_5 (and_5_out, Opcode[5], Opcode[4], ~Opcode[3], Opcode[2]);  // AND_Gate
  or or_1 (Conditional, and_5_out, and_6_out);
  and and_6 (and_6_out, Opcode[5], Opcode[4], Opcode[3], ~Opcode[2], ~Opcode[1]);  // AND_Gate

  // Notes on the sheet:
  //   Shift, add, sub, mov
  //   Load/Store
  //   SP Address
  //   Conditional branch
  //   Data Processing
endmodule

module Data_Processing (
  input  Enable,
  input  [15:0] Instruction,
  output [2:0] Rd,
  output [2:0] Rn,
  output [2:0] Rm,
  output [3:0] ALU_Opcode,
  output [3:0] Flags_Update_Mask
);

  wire and_1_out;
  wire [1:0] multiplexer_1_out;
  wire [2:0] multiplexer_2_out, multiplexer_3_out;

  and and_1 (and_1_out, Instruction[6], ~Instruction[7], Instruction[9]);  // AND_Gate
  Multiplexer #(.select(4), .enable("false")) multiplexer_1 (
    .in0(1'b0), .in1(1'b0), .in2(1'b0), .in3(1'b0), .in4(1'b0), .in5(1'b1), .in6(1'b1), .in7(1'b0),
    .in8(1'b0), .in9(1'b1), .in10(1'b1), .in11(1'b1), .in12(1'b0), .in13(1'b0), .in14(1'b0), .in15(1'b0),
    .out(multiplexer_1_out[0]), .sel(Instruction[9:6]));
  nand nand_1 (multiplexer_1_out[1], Instruction[6], ~Instruction[7], Instruction[8], Instruction[9]);  // NAND_Gate
  Multiplexer #(.width(3), .enable("false")) multiplexer_2 (
    .in0(Instruction[2:0]), .in1(Instruction[5:3]), .out(multiplexer_2_out), .sel(and_1_out));
  Multiplexer #(.width(3), .enable("false")) multiplexer_3 (
    .in0(Instruction[5:3]), .in1(Instruction[2:0]), .out(multiplexer_3_out), .sel(and_1_out));
  Pull_Resistor pull_resistor_1 (.node(Rd));
  assign Rd = Enable ? Instruction[2:0] : 3'bz;  // Controlled_Buffer controlled_buffer_1
  Pull_Resistor pull_resistor_2 (.node(Rn));
  assign Rn = Enable ? multiplexer_2_out : 3'bz;  // Controlled_Buffer controlled_buffer_2
  Pull_Resistor pull_resistor_3 (.node(Rm));
  assign Rm = Enable ? multiplexer_3_out : 3'bz;  // Controlled_Buffer controlled_buffer_3
  Pull_Resistor pull_resistor_4 (.node(ALU_Opcode));
  assign ALU_Opcode = Enable ? Instruction[9:6] : 4'bz;  // Controlled_Buffer controlled_buffer_4
  Pull_Resistor pull_resistor_5 (.node(Flags_Update_Mask));
  assign Flags_Update_Mask = Enable ? {2'b11, multiplexer_1_out} : 4'bz;  // Controlled_Buffer controlled_buffer_5

  // Notes on the sheet:
  //   Note 2: RSB instruction has Rn as 1st operand.
  //   ADC, SBC, RSB, CMP, CMN
  //   MUL instruction has Rn as 1st operand and Rdm as 2nd operand
  //   RSB ou MUL
  //   For simplification purposes, Rm is used for 1st operand both here and in the ALU.
  //   MUL
  //   Note: instructions that does not save the result will still have the second operand as the destination register, the ALU will copy the second register to the destination register
  //   Pull output low on Enable = 0
endmodule

module Shift_Add_Sub_Mov (
  input  Enable,
  input  [15:0] Instruction,
  output [3:0] Flags_Update_Mask,
  output Carry,
  output Imm32_Enable,
  output [2:0] Rm,
  output [2:0] Rn,
  output [2:0] Rd,
  output [4:0] Imm5,
  output [31:0] Imm32,
  output [3:0] ALU_Opcode
);

  wire and_1_out, and_3_out, and_4_out, and_5_out, and_6_out, and_7_out, and_8_out, or_3_out;
  wire [0:0] and_2_out;
  wire [1:0] or_2_out;
  wire [2:0] multiplexer_2_out, multiplexer_3_out;
  wire [3:0] adder_1_out, adder_2_out, multiplexer_5_out, multiplexer_6_out;
  wire [31:0] bit_extender_1_out, bit_extender_2_out, multiplexer_1_out, multiplexer_4_out, negator_1_out;

  and and_1 (and_1_out, Instruction[11], Instruction[12]);
  assign bit_extender_1_out = {{24{1'b0}}, Instruction[7:0]};  // Bit_Extender bit_extender_1
  and and_2 (and_2_out[0], and_1_out, Instruction[9]);
  Adder #(.width(4)) adder_1 (.a(4'b0010), .b(Instruction[14:11]), .out(adder_1_out), .cin(1'b0));  // open: cout
  or or_1 (or_2_out[1], Instruction[11], Instruction[12], ~Instruction[13]);  // OR_Gate
  and and_3 (and_3_out, or_2_out[1], Instruction[13]);
  and and_4 (and_4_out, Instruction[10], Instruction[11], Instruction[12]);
  and and_5 (and_5_out, ~Instruction[11], ~Instruction[12]);  // AND_Gate
  assign bit_extender_2_out = {{29{1'b0}}, Instruction[8:6]};  // Bit_Extender bit_extender_2
  Multiplexer #(.width(32), .enable("false")) multiplexer_1 (
    .in0(bit_extender_1_out), .in1(negator_1_out), .out(multiplexer_1_out), .sel(and_5_out));
  Negator #(.width(32)) negator_1 (.in(bit_extender_1_out), .out(negator_1_out));
  Adder #(.width(4)) adder_2 (
    .a({3'b000, and_2_out[0]}), .b(adder_1_out), .out(adder_2_out), .cin(1'b0));  // open: cout
  or or_2 (or_2_out[0], and_3_out, and_1_out);
  and and_6 (and_6_out, Instruction[9], Instruction[11], Instruction[12], ~Instruction[13], ~Instruction[14], ~Instruction[15]);  // AND_Gate
  or or_3 (or_3_out, and_4_out, Instruction[13]);
  Multiplexer #(.width(3), .enable("false")) multiplexer_2 (
    .in0(Instruction[5:3]), .in1(Instruction[10:8]), .out(multiplexer_2_out), .sel(Instruction[13]));
  Multiplexer #(.width(3), .enable("false")) multiplexer_3 (
    .in0(Instruction[2:0]), .in1(Instruction[10:8]), .out(multiplexer_3_out), .sel(Instruction[13]));
  Multiplexer #(.width(32), .enable("false")) multiplexer_4 (
    .in0(bit_extender_2_out), .in1(multiplexer_1_out), .out(multiplexer_4_out), .sel(Instruction[13]));
  Multiplexer #(.width(4), .enable("false")) multiplexer_5 (
    .in0(adder_2_out), .in1(multiplexer_6_out), .out(multiplexer_5_out), .sel(Instruction[13]));
  Multiplexer #(.select(2), .width(4), .enable("false")) multiplexer_6 (
    .in0(4'b1001), .in1(4'b1010), .in2(4'b0101), .in3(4'b0110), .out(multiplexer_6_out),
    .sel(Instruction[12:11]));
  and and_7 (and_7_out, Enable, and_1_out);
  and and_8 (and_8_out, Enable, or_3_out);
  assign Flags_Update_Mask = Enable ? {2'b11, or_2_out} : 4'bz;  // Controlled_Buffer controlled_buffer_1
  Pull_Resistor pull_resistor_1 (.node(Flags_Update_Mask));
  and and_9 (Carry, Enable, and_6_out);
  and and_10 (Imm32_Enable, Enable, or_3_out);
  assign Rm = and_7_out ? Instruction[8:6] : 3'bz;  // Controlled_Buffer controlled_buffer_2
  Pull_Resistor pull_resistor_2 (.node(Rm));
  assign Rn = Enable ? multiplexer_2_out : 3'bz;  // Controlled_Buffer controlled_buffer_3
  Pull_Resistor pull_resistor_3 (.node(Rn));
  assign Rd = Enable ? multiplexer_3_out : 3'bz;  // Controlled_Buffer controlled_buffer_4
  Pull_Resistor pull_resistor_4 (.node(Rd));
  assign Imm5 = Enable ? Instruction[10:6] : 5'bz;  // Controlled_Buffer controlled_buffer_5
  Pull_Resistor pull_resistor_5 (.node(Imm5));
  assign Imm32 = and_8_out ? multiplexer_4_out : 32'bz;  // Controlled_Buffer controlled_buffer_6
  Pull_Resistor pull_resistor_6 (.node(Imm32));
  Pull_Resistor pull_resistor_7 (.node(ALU_Opcode));
  assign ALU_Opcode = Enable ? multiplexer_5_out : 4'bz;  // Controlled_Buffer controlled_buffer_7

  // Notes on the sheet:
  //   ADD, SUB
  //   LSL
  //   b11,b12
  //   Note: ALU uses Rn register for shifts. Use Rn instead of Rm for shifts (immediate) here too
  //   Note 3: Imm32_Enable forces the use of the immediate for Rm register
  //   !MOV
  //   Note 2: MOV uses RSB ALU opcode with Imm8 reversed so that it is copied to output register
  //   ADDi, SUBi
  //   Pull output low on Enable = 0
  //   SUB
  //   only ADD and SUB use Rm
  //   Enable carry for SUB since it is reversed in ALU
  //   ALU will use Imm32 instead of Rm
endmodule

module Load_Store (
  input  [15:0] Instruction,
  input  Enable,
  input  Clk,
  input  Reset,
  input  [31:0] Stack_Pointer,
  output Store,
  output Load,
  output PC_Hold,
  output [2:0] Rm,
  output [2:0] Rd,
  output [31:0] RAM_Addr
);

  wire and_1_out, and_2_out, d_ff_1_q, d_ff_1_qn, or_1_out;
  wire [2:0] demultiplexer_1_out0, demultiplexer_1_out1;
  wire [31:0] adder_1_out, bit_extender_1_out;

  and and_1 (and_1_out, ~d_ff_1_q, Instruction[11]);  // AND_Gate
  D_Flip_Flop #(.trigger("falling")) d_ff_1 (
    .D(and_1_out), .clk(Clk), .Q(d_ff_1_q), .Qn(d_ff_1_qn), .reset(or_1_out));  // open: preset
  or or_1 (or_1_out, ~Instruction[11], Reset, ~Enable);  // OR_Gate
  assign bit_extender_1_out = {{24{1'b0}}, Instruction[7:0]};  // Bit_Extender bit_extender_1
  Demultiplexer #(.width(3), .enable("false")) demultiplexer_1 (
    .out0(demultiplexer_1_out0), .out1(demultiplexer_1_out1), .in(Instruction[10:8]), .sel(Instruction[11]));
  and and_2 (and_2_out, d_ff_1_qn, Instruction[11]);
  Adder #(.width(32)) adder_1 (.a(bit_extender_1_out), .b(Stack_Pointer), .out(adder_1_out), .cin(1'b0));  // open: cout
  and and_3 (Store, ~Instruction[11], Enable);  // AND_Gate
  and and_4 (Load, Enable, Instruction[11], d_ff_1_q);
  and and_5 (PC_Hold, Enable, and_2_out);
  assign Rm = Enable ? demultiplexer_1_out0 : 3'bz;  // Controlled_Buffer controlled_buffer_1
  Pull_Resistor pull_resistor_1 (.node(Rm));
  assign Rd = Enable ? demultiplexer_1_out1 : 3'bz;  // Controlled_Buffer controlled_buffer_2
  Pull_Resistor pull_resistor_2 (.node(Rd));
  assign RAM_Addr = Enable ? adder_1_out : 32'bz;  // Controlled_Buffer controlled_buffer_3
  Pull_Resistor pull_resistor_3 (.node(RAM_Addr));

  // Notes on the sheet:
  //   Instruction: pull=down
  //   Delay load and hold PC for 1 cycle for the RAM to send out requested data 
endmodule

module SP_Address (
  input  [31:0] Stack_Pointer,
  input  [15:0] Instruction,
  input  Enable,
  output [31:0] New_Stack_Pointer,
  output Write_Enable
);

  wire and_1_out;
  wire [31:0] adder_1_out, bit_extender_1_out, multiplexer_1_out, subtractor_1_out;

  and and_1 (and_1_out, ~Instruction[8], ~Instruction[9], ~Instruction[10], ~Instruction[11]);  // AND_Gate
  assign bit_extender_1_out = {{25{1'b0}}, Instruction[6:0]};  // Bit_Extender bit_extender_1
  Adder #(.width(32)) adder_1 (.a(Stack_Pointer), .b(bit_extender_1_out), .out(adder_1_out));  // open: cin, cout
  Subtractor #(.width(32)) subtractor_1 (
    .a(Stack_Pointer), .b(bit_extender_1_out), .out(subtractor_1_out));  // open: bin, bout
  Multiplexer #(.width(32), .enable("false")) multiplexer_1 (
    .in0(adder_1_out), .in1(subtractor_1_out), .out(multiplexer_1_out), .sel(Instruction[7]));
  Pull_Resistor pull_resistor_1 (.node(New_Stack_Pointer));
  assign New_Stack_Pointer = Write_Enable ? multiplexer_1_out : 32'bz;  // Controlled_Buffer controlled_buffer_1
  and and_2 (Write_Enable, and_1_out, Enable);

  // Notes on the sheet:
  //   Pull output low on Enable = 0
endmodule

module Flags_APSR (
  input  [3:0] Update_Mask,
  input  [3:0] Flags_In,
  input  Clk,
  input  Rst,
  output [3:0] Flags_Out
);

  wire [3:0] and_1_out, and_2_out, or_1_out;

  assign and_1_out = Flags_Out & ~Update_Mask;  // AND_Gate and_1, 4 bits wide
  assign and_2_out = Update_Mask & Flags_In;  // AND_Gate and_2, 4 bits wide
  Register #(.width(4)) Flags (.D(or_1_out), .en(1'b1), .clk(Clk), .Q(Flags_Out), .clr(Rst));
  assign or_1_out = and_1_out | and_2_out;  // OR_Gate or_1, 4 bits wide
endmodule
