// Logisim project Machine.circ as structural Verilog: 2 circuits, main circuit main
module main (
  input  GPIO_A1,
  input  GPIO_A3,
  input  GPIO_A5,
  input  GPIO_A7,
  input  GPIO_A9,
  input  GPIO_A11,
  input  GPIO_A13,
  input  GPIO_A15,
  input  GPIO_A17,
  input  GPIO_A19,
  input  GPIO_A21,
  input  GPIO_A23,
  input  GPIO_A25,
  input  GPIO_A27,
  input  GPIO_A29,
  input  GPIO_A31,
  input  GPIO_A33,
  input  GPIO_A35,
  input  GPIO_B1,
  input  GPIO_B3,
  input  GPIO_B5,
  input  GPIO_B7,
  input  GPIO_B9,
  input  GPIO_B11,
  input  GPIO_B13,
  input  GPIO_B15,
  input  GPIO_B17,
  input  GPIO_B19,
  input  GPIO_B21,
  input  GPIO_B23,
  input  GPIO_B25,
  input  GPIO_B27,
  input  GPIO_B29,
  input  GPIO_B31,
  input  GPIO_B33,
  input  GPIO_B35,
  output GPIO_A2,
  output GPIO_A4,
  output GPIO_A6,
  output GPIO_A8,
  output GPIO_A10,
  output GPIO_A12,
  output GPIO_A14,
  output GPIO_A16,
  output GPIO_A18,
  output GPIO_A20,
  output GPIO_A22,
  output GPIO_A24,
  output GPIO_A26,
  output GPIO_A28,
  output GPIO_A30,
  output GPIO_A32,
  output GPIO_A34,
  output GPIO_A36,
  output GPIO_B2,
  output GPIO_B4,
  output GPIO_B6,
  output GPIO_B8,
  output GPIO_B10,
  output GPIO_B12,
  output GPIO_B14,
  output GPIO_B16,
  output GPIO_B18,
  output GPIO_B20,
  output GPIO_B22,
  output GPIO_B24,
  output GPIO_B26,
  output GPIO_B28,
  output GPIO_B30,
  output GPIO_B32,
  output GPIO_B34,
  output GPIO_B36
);

  wire and_1_out, and_2_out, and_3_out, and_4_out, button_1_out, Clk, Clk_Button_out, clock_1_out,
       CPU_1_store, decoder_1_out0, decoder_1_out1, decoder_1_out2, decoder_1_out3, decoder_1_out4, KEYB_Eof,
       KEYB_Read, KEYB_ReadEn, or_1_out, Reset, RNG_Read, Rst_Button_out, RST_Signal, TTY_Upd;
  wire [3:0] binairy_to_bcd_converter_1_p2, binairy_to_bcd_converter_1_p3, binairy_to_bcd_converter_1_p4,
       binairy_to_bcd_converter_1_p5;
  wire [4:0] JOY_X, JOY_Y;
  wire [6:0] KEYB_Char, TTY_Char;
  wire [8:0] RAM_Addr;
  wire [15:0] multiplier_1_out, ROM_Addr, ROMa_data;
  wire [31:0] CPU_1_r0, CPU_1_r1, CPU_1_r2, CPU_1_r3, CPU_1_r4, CPU_1_r5, CPU_1_r6, CPU_1_r7, CPU_1_ram_out,
       Dip1, Dip2, Dip3, multiplexer_1_out, multiplexer_2_out, RAMa_dout, random_1_out, register_3_q, Res,
       Screen;
  wire [31:1] undriven_2;
  wire [31:5] undriven_4, undriven_5;
  wire [31:7] undriven, undriven_3;
  wire [31:9] CPU_1_ram_addr;

  Decoder #(.select(4)) decoder_1 (
    .out0(decoder_1_out0), .out1(decoder_1_out1), .out2(decoder_1_out2), .out3(decoder_1_out3),
    .out4(decoder_1_out4), .sel(RAM_Addr[3:0]), .en(and_1_out));  // open: out5, out6, out7, out8, out9, out10, out11, out12, out13, out14, out15
  DipSwitch dipswitch_1 (
    .sw1(Dip1[7]), .sw2(Dip1[6]), .sw3(Dip1[5]), .sw4(Dip1[4]), .sw5(Dip1[3]), .sw6(Dip1[2]), .sw7(Dip1[1]),
    .sw8(Dip1[0]));
  and and_1 (and_1_out, RAM_Addr[8], CPU_1_store);
  // Probe on RAM_Addr[3:0]
  // Probe on Dip1[7:0]
  DipSwitch dipswitch_2 (
    .sw1(Dip2[7]), .sw2(Dip2[6]), .sw3(Dip2[5]), .sw4(Dip2[4]), .sw5(Dip2[3]), .sw6(Dip2[2]), .sw7(Dip2[1]),
    .sw8(Dip2[0]));
  Keyboard keyboard_1 (.clk(Clk), .re(KEYB_ReadEn), .clr(Reset), .avail(KEYB_Eof), .data(KEYB_Char));
  RAM #(.dataWidth(32), .databus("bibus")) RAMa (
    .addr(RAM_Addr[7:0]), .we(and_2_out), .oe(1'b1), .clk(Clk), .din(CPU_1_ram_out), .dout(RAMa_dout));
  and and_2 (and_2_out, ~RAM_Addr[8], CPU_1_store);  // AND_Gate
  // Probe on Dip2[7:0]
  // Probe on RAM_Addr
  Register #(.width(7), .trigger("falling")) register_1 (
    .D(CPU_1_ram_out[6:0]), .en(decoder_1_out0), .clk(Clk), .Q(TTY_Char), .clr(Reset));
  Register #(.width(32)) register_2 (.D(CPU_1_ram_out), .en(decoder_1_out1), .clk(Clk), .Q(Res), .clr(Reset));
  Register #(.width(32)) register_3 (.D(CPU_1_ram_out), .en(decoder_1_out2), .clk(Clk), .Q(register_3_q), .clr(Reset));
  Register #(.width(1)) register_4 (.D(CPU_1_ram_out[0]), .en(decoder_1_out4), .clk(Clk), .Q(RST_Signal), .clr(Reset));
  // Probe on Dip3[7:0]
  DipSwitch dipswitch_3 (
    .sw1(Dip3[7]), .sw2(Dip3[6]), .sw3(Dip3[5]), .sw4(Dip3[4]), .sw5(Dip3[3]), .sw6(Dip3[2]), .sw7(Dip3[1]),
    .sw8(Dip3[0]));
  D_Flip_Flop d_ff_1 (.D(decoder_1_out0), .clk(Clk), .Q(TTY_Upd));  // open: Qn, preset, reset
  Register #(.width(32)) register_5 (.D(register_3_q), .en(and_3_out), .clk(Clk), .Q(Screen), .clr(Reset));
  and and_3 (and_3_out, CPU_1_ram_out[0], decoder_1_out3);
  Joystick #(.bits(5)) joystick_1 (.x(JOY_X), .y(JOY_Y));
  DotMatrix #(.inputtype("row"), .matrixcols(8), .matrixrows(4)) dotmatrix_1 (
    .row0(Screen[7:0]), .row1(Screen[15:8]), .row2(Screen[23:16]), .row3(Screen[31:24]));
  // Probe on RAMa_dout
  D_Flip_Flop d_ff_2 (.D(KEYB_Read), .clk(Clk), .Q(KEYB_ReadEn), .reset(or_1_out));  // open: Qn, preset
  or or_1 (or_1_out, ~KEYB_Read, Reset);  // OR_Gate
  Hex_Digit_Display hex_digit_display_1 (.value(Res[15:12]));  // open: dp
  or or_2 (Clk, clock_1_out, Clk_Button_out, button_1_out);
  Clock clock_1 (.out(clock_1_out));
  Button Clk_Button (.out(Clk_Button_out));
  Button Rst_Button (.out(Rst_Button_out));
  or or_3 (Reset, Rst_Button_out, RST_Signal);
  DotMatrix #(.inputtype("row"), .matrixcols(32), .matrixrows(1)) dotmatrix_2 (.row0(Res));
  Hex_Digit_Display hex_digit_display_2 (.value(Res[7:4]));  // open: dp
  Hex_Digit_Display hex_digit_display_3 (.value(Res[11:8]));  // open: dp
  Multiplexer #(.width(32), .enable("false")) multiplexer_1 (
    .in0(RAMa_dout), .in1(multiplexer_2_out), .out(multiplexer_1_out), .sel(RAM_Addr[8]));
  // Probe on multiplexer_1_out
  ROM #(.addrWidth(16), .dataWidth(16)) ROMa (.addr(ROM_Addr), .data(ROMa_data));
  Hex_Digit_Display hex_digit_display_4 (.value(Res[3:0]));  // open: dp
  // Probe on CPU_1_r1
  // Probe on CPU_1_r0
  // Probe on multiplexer_2_out
  Button button_1 (.out(button_1_out));
  Hex_Digit_Display hex_digit_display_5 (.value(binairy_to_bcd_converter_1_p2));  // open: dp
  // Binairy_to_BCD_converter #(.binvalue(13)) binairy_to_bcd_converter_1: pin names not known; wires that end beside it: Res[12:0], binairy_to_bcd_converter_1_p2, binairy_to_bcd_converter_1_p3, binairy_to_bcd_converter_1_p4, binairy_to_bcd_converter_1_p5
  // Probe on CPU_1_r3
  // Probe on CPU_1_r2
  // Probe on CPU_1_r5
  // Probe on CPU_1_r4
  Random #(.width(32)) random_1 (.next(RNG_Read), .clk(Clk), .out(random_1_out));  // open: clr
  // Probe on Res
  Hex_Digit_Display hex_digit_display_6 (.value(binairy_to_bcd_converter_1_p3));  // open: dp
  Hex_Digit_Display hex_digit_display_7 (.value(binairy_to_bcd_converter_1_p4));  // open: dp
  // Probe on CPU_1_r7
  // Probe on CPU_1_r6
  CPU CPU_1 (
    .ROM_Addr(ROM_Addr), .RAM_In(multiplexer_1_out), .R3(CPU_1_r3), .R7(CPU_1_r7), .R2(CPU_1_r2),
    .R6(CPU_1_r6), .RAM_Addr({CPU_1_ram_addr, RAM_Addr}), .R1(CPU_1_r1), .R5(CPU_1_r5), .ROM_In(ROMa_data),
    .R0(CPU_1_r0), .R4(CPU_1_r4), .Clk(Clk), .RAM_Out(CPU_1_ram_out), .Reset(Reset), .Store(CPU_1_store));
  Hex_Digit_Display hex_digit_display_8 (.value(binairy_to_bcd_converter_1_p5));  // open: dp
  // Probe on CPU_1_ram_out
  Multiplexer #(.select(4), .width(32), .enable("false")) multiplexer_2 (
    .in0({undriven, TTY_Char}), .in1(Res), .in2(register_3_q), .in3(Dip1), .in4(Dip2), .in5(Dip3),
    .in6({undriven_2, KEYB_Eof}), .in7({undriven_3, KEYB_Char}), .in8({undriven_4, JOY_X}),
    .in9({undriven_5, JOY_Y}), .in10(random_1_out), .out(multiplexer_2_out), .sel(RAM_Addr[3:0]));  // open: in11, in12, in13, in14, in15
  TTY tty_1 (.data(TTY_Char), .clk(Clk), .we(TTY_Upd), .clr(Reset));
  Multiplier #(.width(16)) multiplier_1 (.a(16'h2), .b(ROM_Addr), .out(multiplier_1_out));  // open: cin, cout
  // Probe on RAM_Addr
  and and_4 (and_4_out, ~CPU_1_store, RAM_Addr[8]);  // AND_Gate
  Decoder #(.select(4)) decoder_2 (
    .out7(KEYB_Read), .out10(RNG_Read), .sel(RAM_Addr[3:0]), .en(and_4_out));  // open: out0, out1, out2, out3, out4, out5, out6, out8, out9, out11, out12, out13, out14, out15
  Pull_Resistor pull_resistor_1 (.node(multiplexer_2_out));
  // Probe on multiplier_1_out

  // Notes on the sheet:
  //   Clavier
  //   Joystick
  //   MMIO
  //   Hexadécimal
  //   contents of ROMa (hex, n*v repeats v):
  //   b088 2000 9007 8*b09e b08e 9006 2001 9005 9004 2064 9001 de75 defe 9803 2107 1a08 9902 2203 4011 c9
  //   4308 2101 4081 9808 4308 9008 defe defe 9805 2107 1a08 9904 2203 4011 c9 4308 2101 4081 9808 4308
  //   9008 defe defe 2001 9009 defe 980c 2800 d002 defe 980d 9001 defe defe 9805 2107 1a08 9904 2203 4011
  //   c9 4308 2101 4081 9808 4388 9008 defe 2001 2800 d101 defe defe dec0 9801 2871 d103 defe 9805 1e40
  //   9005 de19 9801 2864 d103 defe 9805 1c40 9005 de10 9801 287a d103 defe 9804 1e40 9004 de07 9801 2873
  //   d103 defe 9804 1c40 9004 4*defe 9805 2107 4008 9005 9804 2103 4008 9004 9805 9903 4288 d126 defe
  //   9804 9902 4288 d121 defe 9807 1c40 9007 defe defe 9810 2107 4008 9003 9810 2103 4008 9002 defe 9805
  //   9903 2200 4288 9200 d106 defe 9804 9902 1a40 4241 4148 9000 defe 9800 7c0 2800 d1e3 defe defe dea5
  //   2800 d1e3 defe defe dea4 d1e3 defe defe dea4 9804 9903 4341 9106 de1d 9800 2826 d104 defe 9804 9903
  //   4008 9006 de13 9800 287c d104 defe 9804 9903 4308 9006 de09 9800 285e d104 defe 9804 9903 4048 9006
  //   deff debb 6*defe 980b 2800 d100 defe def9 defe 2001 9009 defe defd
  //   Horloge
  //   Registre résultat
  //   Décimal non signé
  //   Use only 8 bit adresses
  //   Console
  //   VCC 5V
  //   VCC 3.3V
  //   VCC 5V
  //   VCC 3.3V
  //   GROUND
  //   GROUND
  //   GROUND
  //   GROUND
endmodule

module CPU (
  input  [31:0] RAM_In,
  input  [15:0] ROM_In,
  input  Clk,
  input  Reset,
  output [31:0] R3,
  output [31:0] R7,
  output [31:0] R2,
  output [31:0] R6,
  output [31:0] R1,
  output [31:0] R5,
  output [31:0] R0,
  output [31:0] R4,
  output [15:0] ROM_Addr,
  output [31:0] RAM_Addr,
  output Store,
  output [31:0] RAM_Out
);

  wire Controller_1_carry, Controller_1_dp_shift, Controller_1_imm32_enable, Controller_1_load;
  wire [2:0] Controller_1_rd, Controller_1_rm, Controller_1_rn;
  wire [3:0] ALU_1_flags, Controller_1_alu_opcode;
  wire [4:0] Controller_1_imm5, multiplexer_3_out;
  wire [31:0] ALU_1_s, Controller_1_imm32, multiplexer_1_out, multiplexer_2_out, Regs_1_bout;

  // Probe on Controller_1_rd
  // Probe on multiplexer_1_out
  Multiplexer #(.width(32), .enable("false")) multiplexer_1 (
    .in0(ALU_1_s), .in1(RAM_In), .out(multiplexer_1_out), .sel(Controller_1_load));
  Controller Controller_1 (
    .Rm(Controller_1_rm), .ALU_Opcode(Controller_1_alu_opcode), .Rn(Controller_1_rn),
    .Imm32_Enable(Controller_1_imm32_enable), .Imm32(Controller_1_imm32), .Rd(Controller_1_rd),
    .Flags(ALU_1_flags), .Imm5(Controller_1_imm5), .PC(ROM_Addr), .Inst(ROM_In),
    .DP_Shift(Controller_1_dp_shift), .Carry(Controller_1_carry), .RAM_Addr(RAM_Addr),
    .Load(Controller_1_load), .Store(Store), .Clk(Clk), .Reset(Reset));
  // Probe on Controller_1_rm
  // Probe on Controller_1_rn
  BancRegistre Regs_1 (
    .Clk(Clk), .Reset(Reset), .DataIn(multiplexer_1_out), .RegB(Controller_1_rn), .AOut(RAM_Out), .R0(R0),
    .R1(R1), .R2(R2), .R3(R3), .R4(R4), .R5(R5), .R6(R6), .R7(R7), .RegA(Controller_1_rm),
    .RegDest(Controller_1_rd), .BOut(Regs_1_bout));
  // Probe on RAM_Out
  Multiplexer #(.width(32), .enable("false")) multiplexer_2 (
    .in0(RAM_Out), .in1(Controller_1_imm32), .out(multiplexer_2_out), .sel(Controller_1_imm32_enable));
  Multiplexer #(.width(5), .enable("false")) multiplexer_3 (
    .in0(RAM_Out[4:0]), .in1(Controller_1_imm5), .out(multiplexer_3_out), .sel(Controller_1_dp_shift));
  // Probe on Regs_1_bout
  ALU ALU_1 (
    .S(ALU_1_s), .Flags(ALU_1_flags), .A(multiplexer_2_out), .B(Regs_1_bout), .Shift(multiplexer_3_out),
    .CarryIn(Controller_1_carry), .Codop(Controller_1_alu_opcode));
  // Probe on ALU_1_s
endmodule
